# Fritzing sketch 24 V Step Down Board (saved by Fritzing 0.9.3b)
circuit board: 3.8cm x 1.8cm
breadboards: 1

parts:
  24_V = Screw terminal - 2 pins [package=THT]
  5_V = Screw terminal - 2 pins [package=THT]
  C1 = Electrolytic Capacitor [capacitance=1µF package="100 mil [THT, electrolytic]"]
  J3 = male pin header, 5 pins [form="♂ (male)"]
  J4 = female pin header, 2 pins [form="♀ (female)"]

nets:
  N1: 24_V.pin1, 5_V.pin1, C1.-, J3.pin4
  N2: 24_V.pin2, C1.+, J3.pin3
  N3: 5_V.pin2, J3.pin5
  N4: J3.pin1, J4.pin2
  N5: J3.pin2, J4.pin1
